// Logisim project SimpleCPU.circ as structural Verilog: 6 circuits, main circuit main
module main (
);

  wire clock_1_out, clock_2_out, clock_3_out, not_1_out;
  wire [1:0] bit_extender_2_out;
  wire [7:0] bit_extender_1_out, multiplexer_1_out, pc_1_out, ram_1_data, reggroup_1_to_alu,
       reggroup_1_to_mem, simplealu_1_out_4;
  wire [31:0] rom_1_data;

  Clock clock_1 (.out(clock_1_out));
  PC pc_1 (.CLK(clock_1_out), .Out(pc_1_out));
  ROM #(.dataWidth(32)) rom_1 (.addr(pc_1_out), .data(rom_1_data));  // open: sel
  Bit_Extender #(.in_width(10), .out_width(8)) bit_extender_1 (.in(rom_1_data[15:6]), .out(bit_extender_1_out));
  Clock clock_2 (.out(clock_2_out));
  Bit_Extender #(.in_width(6), .out_width(2)) bit_extender_2 (.in(rom_1_data[5:0]), .out(bit_extender_2_out));
  RegGroup reggroup_1 (
    .ADDR1(rom_1_data[25:21]), .\数据 (multiplexer_1_out), .ADDR2(rom_1_data[20:16]),
    .\REG写允许 (rom_1_data[31]), .\时钟 (clock_2_out), .TO_ALU(reggroup_1_to_alu), .TO_MEM(reggroup_1_to_mem));
  Multiplexer #(.width(8)) multiplexer_1 (
    .in0(simplealu_1_out_4), .in1(ram_1_data), .out(multiplexer_1_out), .sel(rom_1_data[30]));  // open: en
  SimpleALU simplealu_1 (
    .OP(bit_extender_2_out), .A(reggroup_1_to_alu), .B(bit_extender_1_out), .out_4(simplealu_1_out_4));
  Clock clock_3 (.out(clock_3_out));
  RAM #(.bus("separate")) ram_1 (
    .addr(simplealu_1_out_4), .din(reggroup_1_to_mem), .data(ram_1_data), .str(rom_1_data[29]),
    .clk(clock_3_out), .ld(not_1_out));  // open: sel, clr
  not not_1 (not_1_out, rom_1_data[29]);

  // Notes on the sheet:
  //   contents of rom_1 (hex, n*v repeats v):
  //   80e00082 80e10142 60010002 80210082 60010042 c0010002 80210042 60010002 c0010042 80210103 60010042
endmodule

module AU (
  input  OP,
  input  [7:0] A,
  input  [7:0] B,
  output [7:0] out_4
);

  wire [7:0] adder_1_out, multiplexer_1_out, not_1_out;

  assign not_1_out = ~B;  // NOT_Gate not_1, 8 bits wide
  Adder adder_1 (.a(not_1_out), .b(8'h1), .out(adder_1_out));  // open: cin, cout
  Multiplexer #(.width(8)) multiplexer_1 (.in0(B), .in1(adder_1_out), .out(multiplexer_1_out), .sel(OP));  // open: en
  Adder adder_2 (.a(A), .b(multiplexer_1_out), .out(out_4));  // open: cin, cout
endmodule

module LU (
  input  OP,
  input  [7:0] A,
  input  [7:0] B,
  output [7:0] out_4
);

  wire [7:0] and_1_out, or_1_out;

  assign and_1_out = A & B;  // AND_Gate and_1, 8 bits wide
  assign or_1_out = A | B;  // OR_Gate or_1, 8 bits wide
  Multiplexer #(.width(8)) multiplexer_1 (.in0(and_1_out), .in1(or_1_out), .out(out_4), .sel(OP));  // open: en
endmodule

module SimpleALU (
  input  [1:0] OP,
  input  [7:0] A,
  input  [7:0] B,
  output [7:0] out_4
);

  wire [7:0] au_1_out_4, lu_1_out_4;

  AU au_1 (.OP(OP[0]), .A(A), .B(B), .out_4(au_1_out_4));
  LU lu_1 (.OP(OP[0]), .A(A), .B(B), .out_4(lu_1_out_4));
  Multiplexer #(.width(8)) multiplexer_1 (.in0(lu_1_out_4), .in1(au_1_out_4), .out(out_4), .sel(OP[1]));  // open: en
endmodule

module RegGroup (
  input  [4:0] ADDR1,
  input  [7:0] \数据 ,
  input  [4:0] ADDR2,
  input  \REG写允许 ,
  input  \时钟 ,
  output [7:0] TO_ALU,
  output [7:0] TO_MEM
);

  wire and_1_out, and_2_out, and_3_out, and_4_out, and_5_out, and_6_out, and_7_out, and_8_out,
       decoder_1_out0, decoder_1_out1, decoder_1_out2, decoder_1_out3, decoder_1_out4, decoder_1_out5,
       decoder_1_out6, decoder_1_out7;
  wire [7:0] register_1_q, register_2_q, register_3_q, register_4_q, register_5_q, register_6_q, register_7_q;

  Decoder #(.select(3)) decoder_1 (
    .out0(decoder_1_out0), .out1(decoder_1_out1), .out2(decoder_1_out2), .out3(decoder_1_out3),
    .out4(decoder_1_out4), .out5(decoder_1_out5), .out6(decoder_1_out6), .out7(decoder_1_out7),
    .sel(ADDR2[2:0]));  // open: en
  and and_1 (and_1_out, decoder_1_out0, \REG写允许 );
  and and_2 (and_2_out, decoder_1_out1, \REG写允许 );
  and and_3 (and_3_out, decoder_1_out2, \REG写允许 );
  and and_4 (and_4_out, decoder_1_out3, \REG写允许 );
  and and_5 (and_5_out, decoder_1_out4, \REG写允许 );
  and and_6 (and_6_out, decoder_1_out5, \REG写允许 );
  and and_7 (and_7_out, decoder_1_out6, \REG写允许 );
  and and_8 (and_8_out, decoder_1_out7, \REG写允许 );
  Register register_1 (.D(\数据 ), .en(and_1_out), .Q(register_1_q), .clk(\时钟 ));  // open: clr
  Register register_2 (.D(\数据 ), .en(and_2_out), .Q(register_2_q), .clk(\时钟 ));  // open: clr
  Register register_3 (.D(\数据 ), .en(and_3_out), .Q(register_3_q), .clk(\时钟 ));  // open: clr
  Register register_4 (.D(\数据 ), .en(and_4_out), .Q(register_4_q), .clk(\时钟 ));  // open: clr
  Register register_5 (.D(\数据 ), .en(and_5_out), .Q(register_5_q), .clk(\时钟 ));  // open: clr
  Register register_6 (.D(\数据 ), .en(and_6_out), .Q(register_6_q), .clr(\时钟 ));  // open: clk
  Register register_7 (.D(\数据 ), .en(and_7_out), .Q(register_7_q), .clk(\时钟 ));  // open: clr
  Register register_8 (.D(\数据 ), .en(and_8_out), .Q(register_4_q), .clk(\时钟 ));  // open: clr
  Multiplexer #(.select(3), .width(8)) multiplexer_1 (
    .in0(register_1_q), .in1(register_2_q), .in2(register_3_q), .in3(register_4_q), .in4(register_5_q),
    .in5(register_6_q), .in6(register_7_q), .in7(register_4_q), .out(TO_ALU), .sel(ADDR1[2:0]));  // open: en
  Multiplexer #(.select(3), .width(8)) multiplexer_2 (
    .in0(register_1_q), .in1(register_2_q), .in2(register_3_q), .in3(register_4_q), .in4(register_5_q),
    .in5(register_6_q), .in6(register_7_q), .in7(register_4_q), .out(TO_MEM), .sel(ADDR2[2:0]));  // open: en
endmodule

module PC (
  input  CLK,
  output [7:0] Out
);

  wire [7:0] adder_1_out;

  Register register_1 (.D(adder_1_out), .Q(Out), .clk(CLK));  // open: en, clr
  Adder adder_1 (.a(Out), .b(8'h1), .out(adder_1_out));  // open: cin, cout
endmodule
